# Fritzing sketch circuit (saved by Fritzing 0.9.3b)

parts:
  RTC = ZS-042 RTC Module
  Joystick = Thumb Joystick
  RPI_2040 = Adafruit Feather RP2040 [part_number="Adafruit #4884"]
  3_3V_Converter = RioRand LM2596
  5V_Converter = RioRand LM2596
  12V_Power = Battery block 9V
  HM-10 = Bluetooth HC-05 Macho
  DISPLAY_SPI = female pin header, 4 pins [form="♀ (female)"]
  I2C = female pin header, 2 pins [form="♀ (female)"]
  SD_CARD = SparkFun - microSD Transflash
  TDS_Analog = female pin header, 1 pin [form="♀ (female)"]
  NeoPixel = female pin header, 1 pin [form="♀ (female)"]
  MotorDriver = female pin header, 3 pins [form="♀ (female)"]

nets:
  GND: RTC.GND, Joystick.GND, 5V_Converter.Pin_4, HM-10.GND, SD_CARD.GND, MotorDriver.pin3
  VCC: RTC.VCC, Joystick.VCC, 5V_Converter.Pin_3, HM-10.VCC, SD_CARD.VCC, MotorDriver.pin2
  N1: RTC.SDA, RPI_2040.D24, I2C.pin1
  N2: RTC.SCL, RPI_2040.D25, I2C.pin2
  N3: Joystick.SEL, RPI_2040.D11
  N4: Joystick.HORZ, RPI_2040.A3
  N5: Joystick.VERT, RPI_2040.A2
  N6: RPI_2040.D4, NeoPixel.pin1
  N7: RPI_2040.MISO, DISPLAY_SPI.pin3, SD_CARD.DO
  N8: RPI_2040.MOSI, DISPLAY_SPI.pin2, SD_CARD.DI
  N9: RPI_2040.SCK, DISPLAY_SPI.pin1, SD_CARD.SCK
  N10: RPI_2040.A1, TDS_Analog.pin1
  N11: RPI_2040.GND, 3_3V_Converter.Pin_4
  N12: RPI_2040.+3V3, 3_3V_Converter.Pin_3
  N13: RPI_2040.D12, MotorDriver.pin1
  N14: RPI_2040.D10, HM-10.RXD
  N15: RPI_2040.D9, HM-10.TXD
  N16: RPI_2040.D6, DISPLAY_SPI.pin4
  N17: RPI_2040.D5, SD_CARD.CS
  N18: 3_3V_Converter.Pin_1, 5V_Converter.Pin_1, 12V_Power.+
  N19: 3_3V_Converter.Pin_2, 5V_Converter.Pin_2, 12V_Power.-

notes:
  5V Conveter
  3.3V Conveter
  MISO
  MOSI
  SCLK
  CS
  SDA
  SCL
  HM-10 BLE
  SD Module
  RTC
  Joystick
  RPI PICO
  DISPLAY SPI
  TDS Analog
  GND
  5V
  Data
  NeoPixel
  EN1
  IN1/2
  IN2/1
  MotorDriver

custom parts:
  Adafruit Feather RP2040: A new chip means a new Feather, and the Raspberry Pi RP2040 is no exception. When we saw this chip we thought "this chip is going to be awesome when we give it the Feather Treatment" and so we did! This Feather features the RP2040, and all niceties you know and love about Feather Measures 2.0" x 0.9" x 0.28" (50.8mm x 22.8mm x 7mm) without headers soldered in Light as a (large?) feather - 5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
