# Fritzing sketch circuit_mega (saved by Fritzing 0.9.3b)

parts:
  Joystick = Thumb Joystick
  3_3V_Converter = RioRand LM2596
  5V_Converter = RioRand LM2596
  12V_Power = Battery block 9V
  HM-10 = Bluetooth HC-05 Macho
  DISPLAY_SPI = female pin header, 4 pins [form="♀ (female)"]
  I2C = female pin header, 2 pins [form="♀ (female)"]  # not connected
  SD_CARD = SparkFun - microSD Transflash
  TDS_Analog = female pin header, 1 pin [form="♀ (female)"]
  NeoPixel = female pin header, 1 pin [form="♀ (female)"]
  MotorDriver = female pin header, 3 pins [form="♀ (female)"]
  Arduino_MEGA = Arduino Mega 2560 (Rev3)
  RTC = female pin header, 5 pins [form="♀ (female)"]
  Temp_Sensor = female pin header, 3 pins [form="♀ (female)"]
  R1 = Resistor [tolerance=±5% resistance=4.7k package=THT]

nets:
  GND: Joystick.GND, 5V_Converter.Pin_4, HM-10.GND, SD_CARD.GND, MotorDriver.pin3, Arduino_MEGA.GND, RTC.pin4, Temp_Sensor.pin1
  VCC: Joystick.VCC, 5V_Converter.Pin_3, HM-10.VCC, SD_CARD.VCC, MotorDriver.pin2, Arduino_MEGA.5V, RTC.pin5, Temp_Sensor.pin3, R1.Pin_1
  N1: 3_3V_Converter.Pin_1, 5V_Converter.Pin_1, 12V_Power.+
  N2: 3_3V_Converter.Pin_2, 5V_Converter.Pin_2, 12V_Power.-
  N3: DISPLAY_SPI.pin1, SD_CARD.SCK, Arduino_MEGA.D13_PWM
  N4: DISPLAY_SPI.pin2, SD_CARD.DI, Arduino_MEGA.D11_PWM
  N5: DISPLAY_SPI.pin3, SD_CARD.DO, Arduino_MEGA.D12_PWM
  N6: SD_CARD.CS, Arduino_MEGA.D4_PWM
  N7: TDS_Analog.pin1, Arduino_MEGA.A0
  N8: NeoPixel.pin1, Arduino_MEGA.D3_PWM
  N9: MotorDriver.pin1, Arduino_MEGA.D5_PWM
  N10: Arduino_MEGA.D8_PWM, RTC.pin1
  N11: Arduino_MEGA.D1_TX0, RTC.pin2
  N12: Arduino_MEGA.D2_PWM, Temp_Sensor.pin2, R1.Pin_0
  N13: Arduino_MEGA.D6_PWM, RTC.pin3

notes:
  5V Conveter
  3.3V Conveter
  MISO
  MOSI
  SCLK
  CS
  SDA
  SCL
  HM-10 BLE
  SD Module
  RTC
  Joystick
  Arduino MEGA
  DISPLAY SPI
  TDS Analog
  GND
  5V
  Data
  NeoPixel
  EN1
  IN1/2
  IN2/1
  MotorDriver
  VCC
  CLK
  DAT
  RST
  DATA
  Temp Sensor
  4.7K ohm
